// Logisim project LAB 6.11.24.circ as structural Verilog: 1 circuit, main circuit main
module main (
  input  D1,
  input  in_2,
  input  in_3,
  input  D3,
  input  D4,
  input  in_6,
  input  in_7,
  input  in_8,
  input  S,
  input  in_10,
  output out_11,
  output out_12,
  output out_13,
  output out_14
);

  wire clock_1_out, multiplexer_1_out, multiplexer_2_out, multiplexer_3_out, multiplexer_4_out;

  Clock #(.highDuration(2)) clock_1 (.out(clock_1_out));
  D_Flip_Flop d_ff_1 (.D(multiplexer_1_out), .clk(clock_1_out), .Q(out_11), .preset(S), .reset(in_10));  // open: Qn
  Multiplexer #(.select(2)) multiplexer_1 (
    .in0(in_3), .in1(D1), .in2(out_12), .in3(out_11), .out(multiplexer_1_out), .sel({in_7, in_8}));
  Multiplexer #(.select(2)) multiplexer_2 (
    .in0(in_2), .in1(out_14), .in2(out_11), .in3(out_12), .out(multiplexer_2_out), .sel({in_7, in_8}));
  D_Flip_Flop d_ff_2 (.D(multiplexer_2_out), .clk(clock_1_out), .Q(out_12), .preset(S), .reset(in_10));  // open: Qn
  Multiplexer #(.select(2)) multiplexer_3 (
    .in0(D3), .in1(out_14), .in2(out_12), .in3(out_13), .out(multiplexer_3_out), .sel({in_7, in_8}));
  D_Flip_Flop d_ff_3 (.D(multiplexer_3_out), .clk(clock_1_out), .Q(out_13), .preset(S), .reset(in_10));  // open: Qn
  Multiplexer #(.select(2)) multiplexer_4 (
    .in0(D4), .in1(in_6), .in2(out_13), .in3(out_14), .out(multiplexer_4_out), .sel({in_7, in_8}));
  D_Flip_Flop d_ff_4 (.D(multiplexer_4_out), .clk(clock_1_out), .Q(out_14), .preset(S), .reset(in_10));  // open: Qn

  // Notes on the sheet:
  //   D2
endmodule
